# Fritzing sketch juke (saved by Fritzing 0.9.2b)
circuit board: 12.7cm x 20.3cm
breadboards: 2

parts:
  J1 = female pin header, 20 pins [form="♀ (female)"]
  Q1 = TRANSISTOR_NPN [package=to-92]
  Q2 = TRANSISTOR_NPN [package=to-92]
  Q3 = TRANSISTOR_NPN [package=to-92]
  Q4 = TRANSISTOR_NPN [package=to-92]
  R1 = Resistor [tolerance=±5% resistance=1k power=0pW package=THT]
  R2 = Resistor [tolerance=±5% resistance=1k power=0pW package=THT]
  R4 = Resistor [tolerance=±5% resistance=1k power=0pW package=THT]
  R5 = Resistor [tolerance=±20% resistance=10k package="0402 [SMD]"]
  R6 = Resistor [tolerance=±20% resistance=10k package="0402 [SMD]"]
  R7 = Resistor [tolerance=±20% resistance=10k package="0402 [SMD]"]
  R8 = Resistor [tolerance=±5% resistance=1k power=0pW package=THT]
  R9 = Resistor [tolerance=±5% resistance=100k package=THT]
  R10 = Resistor [tolerance=±5% resistance=100k package=THT]
  R11 = Resistor [tolerance=±5% resistance=100k package=THT]
  R13 = Resistor [tolerance=±5% resistance=51k package=THT]
  R14 = Resistor [tolerance=±5% resistance=51k package=THT]
  R15 = Resistor [tolerance=±5% resistance=51k package=THT]
  Q5 = TRANSISTOR_NPN [package=to-92]
  Q6 = TRANSISTOR_NPN [package=to-92]
  Q7 = TRANSISTOR_NPN [package=to-92]
  Q8 = TRANSISTOR_NPN [package=to-92]
  R17 = Resistor [tolerance=±5% resistance=1k power=0pW package=THT]
  R18 = Resistor [tolerance=±5% resistance=1k power=0pW package=THT]
  R19 = Resistor [tolerance=±5% resistance=1k power=0pW package=THT]
  R20 = Resistor [tolerance=±5% resistance=1k power=0pW package=THT]
  U1 = Voltage Regulator [package=to220-igo]
  J3 = male pin header, 4 pins [form="♂ (male)"]
  C1 = Electrolytic Capacitor [capacitance=10µF package="100 mil [THT, electrolytic]"]
  J2 = female pin header, 10 pins [form="♀ (female)"]
  J5 = female pin header, 9 pins [form="♀ (female)"]
  C2 = Electrolytic Capacitor [capacitance=10µF package="100 mil [THT, electrolytic]"]
  J7 = male pin header, 8 pins [form="♂ (male)"]  # not connected
  J8 = male pin header, 12 pins [form="♂ (male)"]  # not connected
  J9 = male pin header, 14 pins [form="♂ (male)"]  # not connected
  J10 = male pin header, 10 pins [form="♂ (male)"]
  J11 = male pin header, 8 pins [form="♂ (male)"]
  U2 = RJ45 Jack [package=rj45-8]  # not connected
  R3 = Resistor [tolerance=±20% resistance=10k package=THT]

nets:
  N1: J1.pin2, J11.pin7
  N2: J1.pin3, J10.pin3
  N3: J1.pin4, R20.Pin_0
  N4: J1.pin5, R18.Pin_0, R19.Pin_0
  N5: J1.pin6, R9.Pin_0, R13.Pin_1
  N6: J1.pin8, J1.pin16, Q1.E, Q2.E, Q3.E, Q4.E, R13.Pin_0, R14.Pin_0, R15.Pin_0, Q5.E, Q6.E, Q7.E, Q8.E, U1.IN, J3.pin1, C1.+, J2.pin4, J2.pin6, J5.pin7, C2.+
  N7: J1.pin11, J10.pin1
  N8: J1.pin13, J11.pin1
  N9: J1.pin14, J11.pin6
  N10: J1.pin15, J11.pin5
  N11: J1.pin17, J11.pin2
  N12: J1.pin20, R7.Pin_0, J10.pin10, R3.Pin_0
  N13: Q1.B, R1.Pin_1
  N14: Q1.C, R2.Pin_1, R3.Pin_1
  N15: Q2.B, R2.Pin_0
  N16: Q2.C, R5.Pin_0
  N17: Q3.B, R4.Pin_1
  N18: Q3.C, R7.Pin_1, R8.Pin_1
  N19: Q4.B, R8.Pin_0
  N20: Q4.C, R6.Pin_0
  N21: R1.Pin_0, J5.pin1
  N22: R4.Pin_0, J2.pin10
  N23: R5.Pin_1, R6.Pin_1
  N24: R10.Pin_0, R14.Pin_1, J2.pin2
  N25: R11.Pin_0, R15.Pin_1, J2.pin1
  N26: Q5.B, R20.Pin_1
  N27: Q6.B, R18.Pin_1, R19.Pin_1
  N28: Q8.B, R17.Pin_1
  N29: R17.Pin_0, J2.pin5
  N30: U1.GND, C2.-
  N31: U1.OUT, J3.pin4, C1.-
  N32: J5.pin2, J10.pin4
  N33: J5.pin4, J10.pin2
  N34: J5.pin5, J11.pin4
  N35: J5.pin6, J11.pin3
